# Fritzing sketch Schaltung (saved by Fritzing 0.8.5b)
circuit board: 2cm x 2cm
breadboards: 1

parts:
  Anschluss_an_LED-streifen = RGB LED (com. anode, rbg) [package="5 mm [THT]"]
  Power_plug1 = Power plug
  Q1 = NPN-Transistor [package="TO92 [THT]"]
  Q2 = NPN-Transistor [package="TO92 [THT]"]
  Q3 = NPN-Transistor [package="TO92 [THT]"]
  Arduino_Uno = Arduino Uno (Rev3)
  R1 = Resistor [tolerance=±5% resistance=10k package=THT]
  R2 = Resistor [tolerance=±5% resistance=10k package=THT]
  R3 = Resistor [tolerance=±5% resistance=10k package=THT]

nets (from the breadboard view):
  VCC: Anschluss_an_LED-streifen.red_cathode, Power_plug1.VCC, Arduino_Uno.VIN
  N1: Anschluss_an_LED-streifen.common_anode, Q3.C
  N2: Anschluss_an_LED-streifen.blue_cathode, Q2.C
  N3: Anschluss_an_LED-streifen.green_cathode, Q1.C
  GND: Power_plug1.GND, Q1.E, Q2.E, Q3.E, Arduino_Uno.GND
  N4: Q1.B, R3.Pin_0
  N5: Q2.B, R2.Pin_0
  N6: Q3.B, R1.Pin_0
  N7: Arduino_Uno.D9_PWM, R3.Pin_1
  N8: Arduino_Uno.D10_PWM/SS, R2.Pin_1
  N9: Arduino_Uno.D11_PWM/MOSI, R1.Pin_1

notes:
  Wenn der Arduino High ausgibt ist die LED an wenn er low ausgibt ist sie aus.
  weißer Draht: nur nötig wenn der Arduino über keine eigene Stromversorgung verfügt.
  RGB-LED stellt LED-Streifen da.
  Steuerung für LED-Strifen
